# Fritzing sketch Led_board (saved by Fritzing 0.9.2b)
breadboards: 1

parts:
  Q1 = NPN-Transistor [package="TO92 [THT]"]
  Q2 = NPN-Transistor [package="TO92 [THT]"]
  Q3 = NPN-Transistor [package="TO92 [THT]"]
  R1 = Resistor [tolerance=±5% resistance=1k package=THT]
  R2 = Resistor [tolerance=±5% resistance=1k package=THT]
  R3 = Resistor [tolerance=±5% resistance=1k package=THT]
  Q4 = NPN-Transistor [package="TO92 [THT]"]
  Q5 = NPN-Transistor [package="TO92 [THT]"]
  Q6 = NPN-Transistor [package="TO92 [THT]"]
  R4 = Resistor [tolerance=±5% resistance=1k package=THT]
  R5 = Resistor [tolerance=±5% resistance=1k package=THT]
  R6 = Resistor [tolerance=±5% resistance=1k package=THT]
  Q7 = NPN-Transistor [package="TO92 [THT]"]
  Q8 = NPN-Transistor [package="TO92 [THT]"]
  Q9 = NPN-Transistor [package="TO92 [THT]"]
  R7 = Resistor [tolerance=±5% resistance=1k package=THT]
  R8 = Resistor [tolerance=±5% resistance=1k package=THT]
  R9 = Resistor [tolerance=±5% resistance=1k package=THT]
  Q10 = NPN-Transistor [package="TO92 [THT]"]
  Q11 = NPN-Transistor [package="TO92 [THT]"]
  Q12 = NPN-Transistor [package="TO92 [THT]"]
  R10 = Resistor [tolerance=±5% resistance=1k package=THT]
  R11 = Resistor [tolerance=±5% resistance=1k package=THT]
  R12 = Resistor [tolerance=±5% resistance=1k package=THT]
  Q13 = NPN-Transistor [package="TO92 [THT]"]
  Q14 = NPN-Transistor [package="TO92 [THT]"]
  Q15 = NPN-Transistor [package="TO92 [THT]"]
  R13 = Resistor [tolerance=±5% resistance=1k package=THT]
  R14 = Resistor [tolerance=±5% resistance=1k package=THT]
  R15 = Resistor [tolerance=±5% resistance=1k package=THT]
  Q16 = NPN-Transistor [package="TO92 [THT]"]
  Q17 = NPN-Transistor [package="TO92 [THT]"]
  Q18 = NPN-Transistor [package="TO92 [THT]"]
  R16 = Resistor [tolerance=±5% resistance=1k package=THT]
  R17 = Resistor [tolerance=±5% resistance=1k package=THT]
  R18 = Resistor [tolerance=±5% resistance=1k package=THT]
  Arduino_output = female pin header, 18 pins [form="♀ (female)"]
  back_rigth = female pin header, 3 pins [form="♀ (female)"]
  front_left = female pin header, 3 pins [form="♀ (female)"]
  front_rigth = female pin header, 3 pins [form="♀ (female)"]
  land = female pin header, 3 pins [form="♀ (female)"]
  nav = female pin header, 3 pins [form="♀ (female)"]
  back_left = female pin header, 3 pins [form="♀ (female)"]

nets:
  GND: Q1.E, Q2.E, Q3.E, Q4.E, Q5.E, Q6.E, Q7.E, Q8.E, Q9.E, Q10.E, Q11.E, Q12.E, Q13.E, Q14.E, Q15.E, Q16.E, Q17.E, Q18.E
  N1: Q1.B, R1.Pin_0
  N2: Q1.C, back_left.pin1
  N3: Q2.B, R2.Pin_0
  N4: Q2.C, back_left.pin2
  N5: Q3.B, R3.Pin_0
  N6: Q3.C, back_left.pin3
  N7: R1.Pin_1, Arduino_output.pin1
  N8: R2.Pin_1, Arduino_output.pin2
  N9: R3.Pin_1, Arduino_output.pin3
  N10: Q4.B, R4.Pin_0
  N11: Q4.C, back_rigth.pin1
  N12: Q5.B, R5.Pin_0
  N13: Q5.C, back_rigth.pin2
  N14: Q6.B, R6.Pin_0
  N15: Q6.C, back_rigth.pin3
  N16: R4.Pin_1, Arduino_output.pin4
  N17: R5.Pin_1, Arduino_output.pin5
  N18: R6.Pin_1, Arduino_output.pin6
  N19: Q7.B, R7.Pin_0
  N20: Q7.C, front_left.pin1
  N21: Q8.B, R8.Pin_0
  N22: Q8.C, front_left.pin2
  N23: Q9.B, R9.Pin_0
  N24: Q9.C, front_left.pin3
  N25: R7.Pin_1, Arduino_output.pin7
  N26: R8.Pin_1, Arduino_output.pin8
  N27: R9.Pin_1, Arduino_output.pin9
  N28: Q10.B, R10.Pin_0
  N29: Q10.C, front_rigth.pin1
  N30: Q11.B, R11.Pin_0
  N31: Q11.C, front_rigth.pin2
  N32: Q12.B, R12.Pin_0
  N33: Q12.C, front_rigth.pin3
  N34: R10.Pin_1, Arduino_output.pin10
  N35: R11.Pin_1, Arduino_output.pin11
  N36: R12.Pin_1, Arduino_output.pin12
  N37: Q13.B, R13.Pin_0
  N38: Q13.C, land.pin1
  N39: Q14.B, R14.Pin_0
  N40: Q14.C, land.pin2
  N41: Q15.B, R15.Pin_0
  N42: Q15.C, land.pin3
  N43: R13.Pin_1, Arduino_output.pin13
  N44: R14.Pin_1, Arduino_output.pin14
  N45: R15.Pin_1, Arduino_output.pin15
  N46: Q16.B, R16.Pin_0
  N47: Q16.C, nav.pin1
  N48: Q17.B, R17.Pin_0
  N49: Q17.C, nav.pin2
  N50: Q18.B, R18.Pin_0
  N51: Q18.C, nav.pin3
  N52: R16.Pin_1, Arduino_output.pin16
  N53: R17.Pin_1, Arduino_output.pin17
  N54: R18.Pin_1, Arduino_output.pin18
