# Fritzing sketch Led_pcb (saved by Fritzing 0.9.2b)
circuit board: 8.46667cm x 5.64444cm
breadboards: 1

parts:
  Q1 = NPN-Transistor [package="SOT-23 [SMD]"]
  Q2 = NPN-Transistor [package="SOT-23 [SMD]"]
  Q3 = NPN-Transistor [package="SOT-23 [SMD]"]
  Q4 = NPN-Transistor [package="SOT-23 [SMD]"]
  Q5 = NPN-Transistor [package="SOT-23 [SMD]"]  # not connected
  Q6 = NPN-Transistor [package="SOT-23 [SMD]"]
  Q7 = NPN-Transistor [package="SOT-23 [SMD]"]
  Q8 = NPN-Transistor [package="SOT-23 [SMD]"]
  Q9 = NPN-Transistor [package="SOT-23 [SMD]"]
  Q10 = NPN-Transistor [package="SOT-23 [SMD]"]
  Q11 = NPN-Transistor [package="SOT-23 [SMD]"]
  Q12 = NPN-Transistor [package="SOT-23 [SMD]"]
  Q13 = NPN-Transistor [package="SOT-23 [SMD]"]
  Q14 = NPN-Transistor [package="SOT-23 [SMD]"]
  Q15 = NPN-Transistor [package="SOT-23 [SMD]"]
  Q16 = NPN-Transistor [package="SOT-23 [SMD]"]
  Q17 = NPN-Transistor [package="SOT-23 [SMD]"]
  Q18 = NPN-Transistor [package="SOT-23 [SMD]"]
  R1 = Resistor [tolerance=±5% resistance=220 package="0402 [SMD]"]
  R2 = Resistor [tolerance=±5% resistance=220 package="0402 [SMD]"]
  R3 = Resistor [tolerance=±5% resistance=220 package="0402 [SMD]"]
  R4 = Resistor [tolerance=±5% resistance=220 package="0402 [SMD]"]
  R5 = Resistor [tolerance=±5% resistance=220 package="0402 [SMD]"]  # not connected
  R6 = Resistor [tolerance=±5% resistance=220 package="0402 [SMD]"]
  R7 = Resistor [tolerance=±5% resistance=220 package="0402 [SMD]"]
  R8 = Resistor [tolerance=±5% resistance=220 package="0402 [SMD]"]
  R9 = Resistor [tolerance=±5% resistance=220 package="0402 [SMD]"]
  R10 = Resistor [tolerance=±5% resistance=220 package="0402 [SMD]"]
  R11 = Resistor [tolerance=±5% resistance=220 package="0402 [SMD]"]
  R12 = Resistor [tolerance=±5% resistance=220 package="0402 [SMD]"]
  R13 = Resistor [tolerance=±5% resistance=220 package="0402 [SMD]"]
  R14 = Resistor [tolerance=±5% resistance=220 package="0402 [SMD]"]
  R15 = Resistor [tolerance=±5% resistance=220 package="0402 [SMD]"]
  R16 = Resistor [tolerance=±5% resistance=220 package="0402 [SMD]"]
  R17 = Resistor [tolerance=±5% resistance=220 package="0402 [SMD]"]
  R18 = Resistor [tolerance=±5% resistance=220 package="0402 [SMD]"]

nets:
  N1: Q1.1, R1.Pin_0
  N2: Q2.1, R2.Pin_0
  N3: Q3.1, R3.Pin_0
  N4: Q4.1, R4.Pin_0
  N5: Q6.1, R6.Pin_0
  N6: Q7.1, R7.Pin_0
  N7: Q8.1, R8.Pin_0
  N8: Q9.1, R9.Pin_0
  N9: Q10.1, R10.Pin_0
  N10: Q11.1, R11.Pin_0
  N11: Q12.1, R12.Pin_0
  N12: Q13.1, R13.Pin_0
  N13: Q14.1, R14.Pin_0
  N14: Q15.1, R15.Pin_0
  N15: Q16.1, R16.Pin_0
  N16: Q17.1, R17.Pin_0
  N17: Q18.1, R18.Pin_0
